# Fritzing sketch esp8266-fridge-lights (saved by Fritzing 0.9.3b)
breadboards: 1

parts:
  RGB_SMD_LED1 = SMD RGB LED (WS2812) [package=5050]
  J1 = Power Jack [package=power_jack_pth_lock]
  WeMos_D1_Mini1 = WeMos D1 Mini

nets:
  N1: RGB_SMD_LED1.DIn, WeMos_D1_Mini1.D5
  VDD: RGB_SMD_LED1.VDD, J1.PWR, WeMos_D1_Mini1.5V
  VSS: RGB_SMD_LED1.VSS, J1.GND, WeMos_D1_Mini1.G

notes:
  15x 10 LEDs in zig zag
  top left first pixel, bottom right last pixel
  5V power supply
  WeMos d1 mini (ESP8266 devboard)
  D5: data pin for WS2812b LEDs
  5V: power supply
  G: GND
